# Fritzing sketch NodeMcuRgbwLedDriver (saved by Fritzing 1.0.2b)
circuit board: 3.41824cm x 3.91573cm
breadboards: 1

parts:
  Q1 = Basic FET N-Channel [package="DPak [SMD]"]
  Q2 = Basic FET N-Channel [package="DPak [SMD]"]
  Q3 = Basic FET N-Channel [package="DPak [SMD]"]
  Q4 = Basic FET N-Channel [package="DPak [SMD]"]
  R1 = Resistor [tolerance=±5% power=0.25W resistance=10k package=THT]
  R2 = Resistor [tolerance=±5% power=0.25W resistance=10k package=THT]
  R3 = Resistor [tolerance=±5% power=0.25W resistance=10k package=THT]
  R4 = Resistor [tolerance=±5% power=0.25W resistance=10k package=THT]
  U2 = Voltage Regulator - 5V [package="TO220 [THT]"]
  +12v_RGBW = female pin header, 5 pins [form="♀ (female)"]
  +12v_GND = female pin header, 2 pins [form="♀ (female)"]
  NodeMCU_Inputs = female pin header, 5 pins [form="♀ (female)"]

nets:
  N1: Q1.Gate, R4.Pin_1
  N2: Q1.drain, +12v_RGBW.pin2
  N3: Q1.source, Q2.source, Q3.source, Q4.source
  N4: Q2.Gate, R3.Pin_1
  N5: Q2.drain, +12v_RGBW.pin3
  N6: Q3.Gate, R2.Pin_1
  N7: Q3.drain, +12v_RGBW.pin4
  N8: Q4.Gate, R1.Pin_1
  N9: Q4.drain, +12v_RGBW.pin5
  N10: R1.Pin_0, NodeMCU_Inputs.pin2
  N11: R2.Pin_0, NodeMCU_Inputs.pin3
  N12: R3.Pin_0, NodeMCU_Inputs.pin4
  N13: R4.Pin_0, NodeMCU_Inputs.pin5
  N14: U2.input_voltage, +12v_RGBW.pin1, +12v_GND.pin2
  GND: U2.GND, +12v_GND.pin1
  N15: U2.output_voltage, NodeMCU_Inputs.pin1
